# Fritzing sketch MIDISplitter-hc14-pcb-DIN-50x96 (saved by Fritzing 0.9.3b)
circuit board: 5cm x 9.6cm
circuit board: 4cm x 6cm
breadboards: 1

parts:
  VR = Voltage Regulator [package=to220-igo]
  C3 = Tantalum Capacitor [capacitance=22µF package="200 mil [THT, tantalum]"]
  C4 = Ceramic Capacitor [capacitance=100nF package="100 mil [THT, multilayer]"]
  6N138 = 6N138 DIP - 8 pins [package="DIP (Dual Inline) [THT]"]
  D2 = Rectifier Diode [part_number=1N4001 package="300 mil [THT]"]
  R4 = Resistor [tolerance=±5% resistance=220 package=THT]
  R5 = Resistor [tolerance=±5% resistance=470 package=THT]
  R6 = Resistor [tolerance=±5% resistance=10k package=THT]
  MIDI_IN = DIN-5 jack (MIDI) [part_number=DS-5-01 package=THTw]
  MIDI_OUT1 = DIN-5 jack (MIDI) [part_number=DS-5-01 package=THTw]
  R11 = Resistor [tolerance=±5% resistance=220 package=THT]
  R12 = Resistor [tolerance=±5% resistance=220 package=THT]
  MIDI_OUT2 = DIN-5 jack (MIDI) [part_number=DS-5-01 package=THTw]
  R21 = Resistor [tolerance=±5% resistance=220 package=THT]
  R22 = Resistor [tolerance=±5% resistance=220 package=THT]
  MIDI_OUT3 = DIN-5 jack (MIDI) [part_number=DS-5-01 package=THTw]
  R31 = Resistor [tolerance=±5% resistance=220 package=THT]
  R32 = Resistor [tolerance=±5% resistance=220 package=THT]
  MIDI_OUT4 = DIN-5 jack (MIDI) [part_number=DS-5-01 package=THTw]
  R41 = Resistor [tolerance=±5% resistance=220 package=THT]
  U1 = SN74LS14N [package="DIP14 [THT]"]
  MIDI_OUT5 = DIN-5 jack (MIDI) [part_number=DS-5-01 package=THTw]
  R51 = Resistor [tolerance=±5% resistance=220 package=THT]
  R52 = Resistor [tolerance=±5% resistance=220 package=THT]
  BR = DF01 [package="DFM [THT]"]
  Power_plug1 = Power plug [part_number=DS-210]
  J1 = female pin header, 6 pins [form="♀ (female)"]
  J2 = female pin header, 6 pins [form="♀ (female)"]
  J1_2 = male pin header, 6 pins [form="♂ (male)"]
  J2_2 = male pin header, 6 pins [form="♂ (male)"]
  R42 = Resistor [tolerance=±5% resistance=220 package=THT]

nets:
  9V: VR.IN, C4.1, BR.+
  5V: VR.OUT, C3.+, 6N138.pin8, R5.Pin_0, R11.Pin_0, R21.Pin_0, R31.Pin_0, R41.Pin_0, U1.VCC, R51.Pin_0, J1.pin3, J2.pin3, J1_2.pin3, J2_2.pin3
  GND: VR.GND, C3.-, C4.0, 6N138.pin5, R6.Pin_1, MIDI_OUT1.2, MIDI_OUT2.2, MIDI_OUT3.2, MIDI_OUT4.2, U1.GND, MIDI_OUT5.2, BR.-, J1.pin6, J1_2.pin6
  N1: 6N138.pin2, D2.cathode, R4.Pin_1
  U_IN5: 6N138.pin3, D2.anode, J2_2.pin6
  MIDI_IN: 6N138.pin6, R5.Pin_1, U1.4A
  N2: 6N138.pin7, R6.Pin_0
  U_IN4: R4.Pin_0, J2_2.pin5
  L_IN5: MIDI_IN.5, J2.pin6
  L_IN4: MIDI_IN.4, J2.pin5
  L_OUT1: MIDI_OUT1.5, J2.pin1
  N3: MIDI_OUT1.4, R11.Pin_1
  N4: R12.Pin_0, U1.1Y
  U_OUT1: R12.Pin_1, J2_2.pin1
  L_OUT2: MIDI_OUT2.5, J2.pin2
  N5: MIDI_OUT2.4, R21.Pin_1
  N6: R22.Pin_0, U1.2Y
  U_OUT2: R22.Pin_1, J2_2.pin2
  L_OUT3: MIDI_OUT3.5, J2.pin4
  N7: MIDI_OUT3.4, R31.Pin_1
  N8: R32.Pin_0, U1.3Y
  U_OUT3: R32.Pin_1, J2_2.pin4
  L_OUT4: MIDI_OUT4.5, J1.pin5
  N9: MIDI_OUT4.4, R41.Pin_1
  N10: U1.1A, U1.2A, U1.3A, U1.4Y, U1.5A, U1.6A
  N11: U1.5Y, R42.Pin_0
  N12: U1.6Y, R52.Pin_0
  L_OUT5: MIDI_OUT5.5, J1.pin4
  N13: MIDI_OUT5.4, R51.Pin_1
  U_OUT5: R52.Pin_1, J1_2.pin4
  U_9vDC1: BR.~#2, J1_2.pin1
  U_9vDC2: BR.~#3, J1_2.pin2
  L_9vDC2: Power_plug1.VCC, J1.pin1
  L_9vDC1: Power_plug1.GND, J1.pin2
  U_OUT4: J1_2.pin5, R42.Pin_1

notes:
  MIDI IN
  POWER

custom parts:
  Voltage Regulator: Voltage Regulator Standard L4940V5 5V regulator. IGO (Input Ground Output). ST Microelectronics
  6N138 DIP - 8 pins: A DIP stand-in part for whatever IC you want. With 8 pins on a 300mil dual inline package (DIP) footprint.
  DIN-5 jack (MIDI): Female DIN connector with 5 pins, as used for MIDI and SYNC
  DF01: Single-Phase Bridge Rectifier
  Power plug: power plug
